# Fritzing sketch FindingLychee (saved by Fritzing 0.9.2b)
breadboards: 1

parts:
  Part1 = Arduino Nano (Rev3.0)
  IC1 = 24LC32 [package=THT]
  U3 = GP-2106 [package=gp-2106]
  VCC1 = Battery

nets:
  N1: Part1.D3, U3.TX
  N2: Part1.D4, U3.RX
  N3: Part1.A5, IC1.SCL_-_I2C_Clock
  N4: Part1.A4, IC1.SDA_-_I2C_Data
  N5: IC1.0V, U3.GND, VCC1.-
  N6: IC1.+V, U3.VCC, VCC1.+
